# Fritzing sketch nadajnik_schemat (saved by Fritzing 0.9.3b)
breadboards: 1

parts:
  LED1 = smd LED [color="Red (633nm)" package="0805 [SMD]"]
  R1 = Resistor [tolerance=±5% resistance=330 package="1206 [SMD]"]
  U1 = atmega328 [package=dip]
  XTAL1 = Crystal [frequency="16 Mhz" package=THT]  # not connected
  R2 = Resistor [tolerance=±5% resistance=220 package="1206 [SMD]"]
  VCC1 = Battery

nets:
  N1: LED1.cathode, U1.GND, R2.Pin_0, VCC1.-
  N2: LED1.anode, R1.Pin_1
  N3: U1.RESET, R2.Pin_1
  N4: U1.VCC, VCC1.+
